// Logisim project P0_Q2_1.circ as structural Verilog: 1 circuit, main circuit grf
module grf (
  input  clk,
  input  reset,
  input  WE,
  input  [4:0] A1,
  input  [4:0] A2,
  input  [4:0] A3,
  input  [31:0] WD,
  output [31:0] RD1,
  output [31:0] RD2
);

  wire [31:0] I00, I01, I02, I03, I04, I05, I06, I07, I08, I09, I10, I11, I12, I13, I14, I15, I16, I17, I18,
       I19, I20, I21, I22, I23, I24, I25, I26, I27, I28, I29, I30, I31, O01, O02, O03, O04, O05, O06, O07,
       O08, O09, O10, O11, O12, O13, O14, O15, O16, O17, O18, O19, O20, O21, O22, O23, O24, O25, O26, O27,
       O28, O29, O30, O31;

  Register #(.width(32)) register_1 (.D(I08), .en(1'b1), .Q(O08), .clk(clk), .clr(reset));
  Register #(.width(32)) register_2 (.D(I16), .en(1'b1), .Q(O16), .clk(clk), .clr(reset));
  Register #(.width(32)) register_3 (.D(I24), .en(1'b1), .Q(O24), .clk(clk), .clr(reset));
  Register #(.width(32)) register_4 (.D(I01), .en(1'b1), .Q(O01), .clk(clk), .clr(reset));
  Register #(.width(32)) register_5 (.D(I09), .en(1'b1), .Q(O09), .clk(clk), .clr(reset));
  Register #(.width(32)) register_6 (.D(I17), .en(1'b1), .Q(O17), .clk(clk), .clr(reset));
  Register #(.width(32)) register_7 (.D(I25), .en(1'b1), .Q(O25), .clk(clk), .clr(reset));
  Register #(.width(32)) register_8 (.D(I02), .en(1'b1), .Q(O02), .clk(clk), .clr(reset));
  Register #(.width(32)) register_9 (.D(I10), .en(1'b1), .Q(O10), .clk(clk), .clr(reset));
  Register #(.width(32)) register_10 (.D(I18), .en(1'b1), .Q(O18), .clk(clk), .clr(reset));
  Register #(.width(32)) register_11 (.D(I26), .en(1'b1), .Q(O26), .clk(clk), .clr(reset));
  Multiplexer #(.select(5), .width(32), .enable("false")) multiplexer_1 (
    .in0({32{1'b0}}), .in1(O01), .in2(O02), .in3(O03), .in4(O04), .in5(O05), .in6(O06), .in7(O07), .in8(O08),
    .in9(O09), .in10(O10), .in11(O11), .in12(O12), .in13(O13), .in14(O14), .in15(O15), .in16(O16),
    .in17(O17), .in18(O18), .in19(O19), .in20(O20), .in21(O21), .in22(O22), .in23(O23), .in24(O24),
    .in25(O25), .in26(O26), .in27(O27), .in28(O28), .in29(O29), .in30(O30), .in31(O31), .out(RD1), .sel(A1));
  Register #(.width(32)) register_12 (.D(I03), .en(1'b1), .Q(O03), .clk(clk), .clr(reset));
  Register #(.width(32)) register_13 (.D(I11), .en(1'b1), .Q(O11), .clk(clk), .clr(reset));
  Register #(.width(32)) register_14 (.D(I19), .en(1'b1), .Q(O19), .clk(clk), .clr(reset));
  Register #(.width(32)) register_15 (.D(I27), .en(1'b1), .Q(O27), .clk(clk), .clr(reset));
  Register #(.width(32)) register_16 (.D(I04), .en(1'b1), .Q(O04), .clk(clk), .clr(reset));
  Register #(.width(32)) register_17 (.D(I12), .en(1'b1), .Q(O12), .clk(clk), .clr(reset));
  Register #(.width(32)) register_18 (.D(I20), .en(1'b1), .Q(O20), .clk(clk), .clr(reset));
  Register #(.width(32)) register_19 (.D(I28), .en(1'b1), .Q(O28), .clk(clk), .clr(reset));
  Multiplexer #(.select(5), .width(32), .enable("false")) multiplexer_2 (
    .in0({32{1'b0}}), .in1(O01), .in2(O02), .in3(O03), .in4(O04), .in5(O05), .in6(O06), .in7(O07), .in8(O08),
    .in9(O09), .in10(O10), .in11(O11), .in12(O12), .in13(O13), .in14(O14), .in15(O15), .in16(O16),
    .in17(O17), .in18(O18), .in19(O19), .in20(O20), .in21(O21), .in22(O22), .in23(O23), .in24(O24),
    .in25(O25), .in26(O26), .in27(O27), .in28(O28), .in29(O29), .in30(O30), .in31(O31), .out(RD2), .sel(A2));
  Register #(.width(32)) register_20 (.D(I05), .en(1'b1), .Q(O05), .clk(clk), .clr(reset));
  Register #(.width(32)) register_21 (.D(I13), .en(1'b1), .Q(O13), .clk(clk), .clr(reset));
  Register #(.width(32)) register_22 (.D(I21), .en(1'b1), .Q(O21), .clk(clk), .clr(reset));
  Register #(.width(32)) register_23 (.D(I29), .en(1'b1), .Q(O29), .clk(clk), .clr(reset));
  Demultiplexer #(.select(5), .width(32), .tristate("true")) demultiplexer_1 (
    .out0(I00), .out1(I01), .out2(I02), .out3(I03), .out4(I04), .out5(I05), .out6(I06), .out7(I07),
    .out8(I08), .out9(I09), .out10(I10), .out11(I11), .out12(I12), .out13(I13), .out14(I14), .out15(I15),
    .out16(I16), .out17(I17), .out18(I18), .out19(I19), .out20(I20), .out21(I21), .out22(I22), .out23(I23),
    .out24(I24), .out25(I25), .out26(I26), .out27(I27), .out28(I28), .out29(I29), .out30(I30), .out31(I31),
    .in(WD), .sel(A3), .en(WE));
  Register #(.width(32)) register_24 (.D(I06), .en(1'b1), .Q(O06), .clk(clk), .clr(reset));
  Register #(.width(32)) register_25 (.D(I14), .en(1'b1), .Q(O14), .clk(clk), .clr(reset));
  Register #(.width(32)) register_26 (.D(I22), .en(1'b1), .Q(O22), .clk(clk), .clr(reset));
  Register #(.width(32)) register_27 (.D(I30), .en(1'b1), .Q(O30), .clk(clk), .clr(reset));
  Register #(.width(32)) register_28 (.D(I07), .en(1'b1), .Q(O07), .clk(clk), .clr(reset));
  Register #(.width(32)) register_29 (.D(I15), .en(1'b1), .Q(O15), .clk(clk), .clr(reset));
  Register #(.width(32)) register_30 (.D(I23), .en(1'b1), .Q(O23), .clk(clk), .clr(reset));
  Register #(.width(32)) register_31 (.D(I31), .en(1'b1), .Q(O31), .clk(clk), .clr(reset));

  // Notes on the sheet:
  //   Inputs
  //   Outputs
endmodule
