// Logisim project P0_Q2_2.circ as structural Verilog: 1 circuit, main circuit grf
module grf (
  input  clk,
  input  reset,
  input  WE,
  input  [4:0] A1,
  input  [4:0] A2,
  input  [4:0] A3,
  input  [31:0] WD,
  output [31:0] RD1,
  output [31:0] RD2
);

  wire E00, E01, E02, E03, E04, E05, E06, E07, E08, E09, E10, E11, E12, E13, E14, E15, E16, E17, E18, E19,
       E20, E21, E22, E23, E24, E25, E26, E27, E28, E29, E30, E31;
  wire [31:0] O01, O02, O03, O04, O05, O06, O07, O08, O09, O10, O11, O12, O13, O14, O15, O16, O17, O18, O19,
       O20, O21, O22, O23, O24, O25, O26, O27, O28, O29, O30, O31;

  Register #(.width(32)) register_1 (.D(WD), .en(E08), .Q(O08), .clk(clk), .clr(reset));
  Register #(.width(32)) register_2 (.D(WD), .en(E16), .Q(O16), .clk(clk), .clr(reset));
  Register #(.width(32)) register_3 (.D(WD), .en(E24), .Q(O24), .clk(clk), .clr(reset));
  Register #(.width(32)) register_4 (.D(WD), .en(E01), .Q(O01), .clk(clk), .clr(reset));
  Register #(.width(32)) register_5 (.D(WD), .en(E09), .Q(O09), .clk(clk), .clr(reset));
  Register #(.width(32)) register_6 (.D(WD), .en(E17), .Q(O17), .clk(clk), .clr(reset));
  Register #(.width(32)) register_7 (.D(WD), .en(E25), .Q(O25), .clk(clk), .clr(reset));
  Register #(.width(32)) register_8 (.D(WD), .en(E02), .Q(O02), .clk(clk), .clr(reset));
  Register #(.width(32)) register_9 (.D(WD), .en(E10), .Q(O10), .clk(clk), .clr(reset));
  Register #(.width(32)) register_10 (.D(WD), .en(E18), .Q(O18), .clk(clk), .clr(reset));
  Register #(.width(32)) register_11 (.D(WD), .en(E26), .Q(O26), .clk(clk), .clr(reset));
  Multiplexer #(.select(5), .width(32), .enable("false")) multiplexer_1 (
    .in0({32{1'b0}}), .in1(O01), .in2(O02), .in3(O03), .in4(O04), .in5(O05), .in6(O06), .in7(O07), .in8(O08),
    .in9(O09), .in10(O10), .in11(O11), .in12(O12), .in13(O13), .in14(O14), .in15(O15), .in16(O16),
    .in17(O17), .in18(O18), .in19(O19), .in20(O20), .in21(O21), .in22(O22), .in23(O23), .in24(O24),
    .in25(O25), .in26(O26), .in27(O27), .in28(O28), .in29(O29), .in30(O30), .in31(O31), .out(RD1), .sel(A1));
  Register #(.width(32)) register_12 (.D(WD), .en(E03), .Q(O03), .clk(clk), .clr(reset));
  Register #(.width(32)) register_13 (.D(WD), .en(E11), .Q(O11), .clk(clk), .clr(reset));
  Register #(.width(32)) register_14 (.D(WD), .en(E19), .Q(O19), .clk(clk), .clr(reset));
  Register #(.width(32)) register_15 (.D(WD), .en(E27), .Q(O27), .clk(clk), .clr(reset));
  Register #(.width(32)) register_16 (.D(WD), .en(E04), .Q(O04), .clk(clk), .clr(reset));
  Register #(.width(32)) register_17 (.D(WD), .en(E12), .Q(O12), .clk(clk), .clr(reset));
  Register #(.width(32)) register_18 (.D(WD), .en(E20), .Q(O20), .clk(clk), .clr(reset));
  Register #(.width(32)) register_19 (.D(WD), .en(E28), .Q(O28), .clk(clk), .clr(reset));
  Multiplexer #(.select(5), .width(32), .enable("false")) multiplexer_2 (
    .in0({32{1'b0}}), .in1(O01), .in2(O02), .in3(O03), .in4(O04), .in5(O05), .in6(O06), .in7(O07), .in8(O08),
    .in9(O09), .in10(O10), .in11(O11), .in12(O12), .in13(O13), .in14(O14), .in15(O15), .in16(O16),
    .in17(O17), .in18(O18), .in19(O19), .in20(O20), .in21(O21), .in22(O22), .in23(O23), .in24(O24),
    .in25(O25), .in26(O26), .in27(O27), .in28(O28), .in29(O29), .in30(O30), .in31(O31), .out(RD2), .sel(A2));
  Register #(.width(32)) register_20 (.D(WD), .en(E05), .Q(O05), .clk(clk), .clr(reset));
  Register #(.width(32)) register_21 (.D(WD), .en(E13), .Q(O13), .clk(clk), .clr(reset));
  Register #(.width(32)) register_22 (.D(WD), .en(E21), .Q(O21), .clk(clk), .clr(reset));
  Register #(.width(32)) register_23 (.D(WD), .en(E29), .Q(O29), .clk(clk), .clr(reset));
  Decoder #(.select(5), .disabled(0)) decoder_1 (
    .out0(E00), .out1(E01), .out2(E02), .out3(E03), .out4(E04), .out5(E05), .out6(E06), .out7(E07),
    .out8(E08), .out9(E09), .out10(E10), .out11(E11), .out12(E12), .out13(E13), .out14(E14), .out15(E15),
    .out16(E16), .out17(E17), .out18(E18), .out19(E19), .out20(E20), .out21(E21), .out22(E22), .out23(E23),
    .out24(E24), .out25(E25), .out26(E26), .out27(E27), .out28(E28), .out29(E29), .out30(E30), .out31(E31),
    .sel(A3), .en(WE));
  Register #(.width(32)) register_24 (.D(WD), .en(E06), .Q(O06), .clk(clk), .clr(reset));
  Register #(.width(32)) register_25 (.D(WD), .en(E14), .Q(O14), .clk(clk), .clr(reset));
  Register #(.width(32)) register_26 (.D(WD), .en(E22), .Q(O22), .clk(clk), .clr(reset));
  Register #(.width(32)) register_27 (.D(WD), .en(E30), .Q(O30), .clk(clk), .clr(reset));
  Register #(.width(32)) register_28 (.D(WD), .en(E07), .Q(O07), .clk(clk), .clr(reset));
  Register #(.width(32)) register_29 (.D(WD), .en(E15), .Q(O15), .clk(clk), .clr(reset));
  Register #(.width(32)) register_30 (.D(WD), .en(E23), .Q(O23), .clk(clk), .clr(reset));
  Register #(.width(32)) register_31 (.D(WD), .en(E31), .Q(O31), .clk(clk), .clr(reset));

  // Notes on the sheet:
  //   Inputs
  //   Outputs
endmodule
