// Logisim project P0_Q4_2.circ as structural Verilog: 3 circuits, main circuit fsm
module fsm (
  input  CLR,
  input  [1:0] In,
  output Z
);

  wire clock_1_out;
  wire [1:0] next_1_o0, register_1_q;

  next next_1 (
    .reset(CLR), .b1(register_1_q[1]), .o1(next_1_o0[1]), .b0(register_1_q[0]), .i1(In[1]), .i0(In[0]),
    .o0(next_1_o0[0]));
  Clock clock_1 (.out(clock_1_out));
  out out_1 (.b1(register_1_q[1]), .o(Z), .b0(register_1_q[0]), .i1(In[1]), .i0(In[0]));
  Register #(.width(2)) register_1 (.D(next_1_o0), .en(1'b1), .Q(register_1_q), .clk(clock_1_out), .clr(1'b0));
endmodule

module next (
  input  reset,
  input  b1,
  input  b0,
  input  i1,
  input  i0,
  output o1,
  output o0
);

  wire and_1_out, and_2_out, and_3_out, and_4_out, and_5_out, not_1_out, not_2_out, not_3_out, not_4_out,
       not_5_out, not_6_out, not_7_out, not_8_out, not_9_out, not_10_out, not_11_out, not_12_out, not_13_out,
       not_14_out;

  not not_1 (not_1_out, reset);
  not not_2 (not_2_out, b1);
  not not_3 (not_3_out, i0);
  not not_4 (not_4_out, reset);
  not not_5 (not_5_out, b0);
  not not_6 (not_6_out, i0);
  not not_7 (not_7_out, reset);
  not not_8 (not_8_out, b1);
  not not_9 (not_9_out, i1);
  not not_10 (not_10_out, reset);
  not not_11 (not_11_out, i1);
  not not_12 (not_12_out, reset);
  not not_13 (not_13_out, b0);
  not not_14 (not_14_out, i0);
  and and_1 (and_1_out, not_1_out, not_2_out, b0, not_3_out);
  and and_2 (and_2_out, not_4_out, b1, not_5_out, not_6_out);
  and and_3 (and_3_out, not_7_out, not_8_out, not_9_out, i0);
  and and_4 (and_4_out, not_10_out, b0, not_11_out, i0);
  and and_5 (and_5_out, not_12_out, b1, not_13_out, not_14_out);
  or or_1 (o1, and_1_out, and_2_out);
  or or_2 (o0, and_3_out, and_4_out, and_5_out);
endmodule

module out (
  input  b1,
  input  b0,
  input  i1,
  input  i0,
  output o
);

  wire not_1_out, not_2_out;

  not not_1 (not_1_out, b0);
  and and_1 (o, b1, not_1_out, not_2_out);
  not not_2 (not_2_out, i0);
endmodule
