// Logisim project P0_ftoi_wrong.circ as structural Verilog: 1 circuit, main circuit ftoi
module ftoi (
  input  [15:0] float,
  output [31:0] \int 
);

  wire and_1_out, comparator_1_lt, nor_1_out, or_1_out;
  wire [4:0] bitfinder_1_index, subtractor_1_out;
  wire [31:0] multiplexer_1_out, negator_1_out, shifter_1_out, shifter_2_out;

  Negator #(.width(32)) negator_1 (.in(shifter_2_out), .out(negator_1_out));
  Multiplexer #(.width(32), .enable("false")) multiplexer_1 (
    .in0(shifter_2_out), .in1(negator_1_out), .out(multiplexer_1_out), .sel(float[15]));
  and and_1 (and_1_out, float[10], float[11], float[12], float[13], float[14]);
  or or_1 (or_1_out, and_1_out, nor_1_out, comparator_1_lt);
  nor nor_1 (nor_1_out, float[10], float[11], float[12], float[13], float[14]);
  Comparator #(.width(5), .mode("unsigned")) comparator_1 (
    .a(float[14:10]), .b(5'b01111), .lt(comparator_1_lt));  // open: gt, eq
  Subtractor #(.width(5)) subtractor_1 (.a(float[14:10]), .b(5'b01111), .out(subtractor_1_out));  // open: bin, bout
  BitFinder #(.width(32)) bitfinder_1 (.in({22'h1, float[9:0]}), .index(bitfinder_1_index));  // open: found
  Multiplexer #(.width(32), .enable("false")) multiplexer_2 (
    .in0(multiplexer_1_out), .in1({32{1'b0}}), .out(\int ), .sel(or_1_out));
  Shifter #(.width(32), .shift("lr")) shifter_1 (
    .in({22'h1, float[9:0]}), .\dist (bitfinder_1_index), .out(shifter_1_out));
  Shifter #(.width(32)) shifter_2 (.in(shifter_1_out), .\dist (subtractor_1_out), .out(shifter_2_out));

  // Notes on the sheet:
  //   Inf or NaN
  //   Denormalized
  //   Right Shift
  //   Get E
endmodule
