// Logisim project P3_tester.circ as structural Verilog: 1 circuit, main circuit main
module main (
  output [31:0] Exam_Instr,
  output [31:0] Exam_PC,
  output Exam_RegWrite,
  output [4:0] Exam_RegAddr,
  output [31:0] Exam_RegData,
  output halt,
  output Exam_MemWrite,
  output [31:0] Exam_MemAddr,
  output [31:0] Exam_MemData
);

  wire clock_1_out, comparator_1_gt;
  wire [9:0] counter_1_q;

  Clock clock_1 (.out(clock_1_out));
  Counter #(.width(10), .max('h3ff), .ongoal("stay")) counter_1 (
    .Q(counter_1_q), .carry(halt), .clk(clock_1_out));  // open: load, D, count, clr
  P3_Full_main main_1 (
    .Input(comparator_1_gt), .Exam_Instr(Exam_Instr), .Exam_PC(Exam_PC), .Exam_RegWrite(Exam_RegWrite),
    .Exam_RegAddr(Exam_RegAddr), .Exam_RegData(Exam_RegData), .Exam_MemWrite(Exam_MemWrite),
    .Exam_MemAddr(Exam_MemAddr), .Exam_MemData(Exam_MemData));
  Comparator #(.width(10), .mode("unsigned")) comparator_1 (
    .a(10'h4), .b(counter_1_q), .gt(comparator_1_gt));  // open: eq, lt
endmodule
