// Logisim project P3_Full.circ as structural Verilog: 12 circuits, main circuit main
module main (
  input  Input,
  output [31:0] Exam_Instr,
  output [31:0] Exam_PC,
  output Exam_RegWrite,
  output [4:0] Exam_RegAddr,
  output [31:0] Exam_RegData,
  output Exam_MemWrite,
  output [31:0] Exam_MemAddr,
  output [31:0] Exam_MemData
);

  wire alu_1_comp, ALUrtMUX, clk;
  wire [1:0] EXTSel, GRFA3MUX, GRFWDMUX, NPCSel, OPSel;
  wire [2:0] CompSel, DMSel, FuncSel;
  wire [4:0] shamt, spl_1_rd, spl_1_rs, spl_1_rt;
  wire [5:0] spl_1_funct, spl_1_opcode;
  wire [15:0] spl_1_imm16;
  wire [25:0] spl_1_instr_index;
  wire [31:0] adder_1_out, dm_1_d_read, ext_1_ext, grf_1_rd1, multiplexer_3_out;

  Clock clock_1 (.out(clk));
  IFU ifu_1 (
    .RESET(Input), .Instr(Exam_Instr), .PC(Exam_PC), .clk(clk), .offset(spl_1_imm16),
    .instr_index(spl_1_instr_index), .instr_register(grf_1_rd1), .NPCSel(NPCSel), .BranchComp(alu_1_comp));
  SPL spl_1 (
    .Instr(Exam_Instr), .funct(spl_1_funct), .shamt(shamt), .rd(spl_1_rd), .rt(spl_1_rt), .rs(spl_1_rs),
    .opcode(spl_1_opcode), .imm16(spl_1_imm16), .instr_index(spl_1_instr_index));
  CTRL ctrl_1 (
    .opcode(spl_1_opcode), .OPSel(OPSel), .funct(spl_1_funct), .rt(spl_1_rt), .EXTSel(EXTSel), .DMSel(DMSel),
    .NPCSel(NPCSel), .FuncSel(FuncSel), .CompSel(CompSel), .GRFWE(Exam_RegWrite), .DMWE(Exam_MemWrite),
    .GRFA3MUX(GRFA3MUX), .GRFWDMUX(GRFWDMUX), .ALUrtMUX(ALUrtMUX));
  Multiplexer #(.select(2), .width(5), .enable("false")) multiplexer_1 (
    .in0({5{1'b0}}), .in1(spl_1_rd), .in2(spl_1_rt), .in3({5{1'b1}}), .out(Exam_RegAddr), .sel(GRFA3MUX));
  Adder #(.width(32)) adder_1 (.a(Exam_PC), .b(32'h4), .out(adder_1_out));  // open: cin, cout
  EXT ext_1 (.imm16(spl_1_imm16), .in_2(EXTSel), .EXT(ext_1_ext));
  Multiplexer #(.select(2), .width(32), .enable("false")) multiplexer_2 (
    .in0(Exam_MemAddr), .in1(ext_1_ext), .in2(dm_1_d_read), .in3(adder_1_out), .out(Exam_RegData),
    .sel(GRFWDMUX));
  GRF grf_1 (
    .clk(clk), .reset(Input), .WE(Exam_RegWrite), .A1(spl_1_rs), .A2(spl_1_rt), .A3(Exam_RegAddr),
    .WD(Exam_RegData), .RD1(grf_1_rd1), .RD2(Exam_MemData));
  Multiplexer #(.width(32), .enable("false")) multiplexer_3 (
    .in0(Exam_MemData), .in1(ext_1_ext), .out(multiplexer_3_out), .sel(ALUrtMUX));
  ALU alu_1 (
    .rs(grf_1_rd1), .OP(Exam_MemAddr), .Comp(alu_1_comp), .rt(multiplexer_3_out), .shamt(shamt),
    .CompSel(CompSel), .OPSel(OPSel), .FuncSel(FuncSel));
  DM dm_1 (
    .RESET(Input), .clk(clk), .WE(Exam_MemWrite), .DMSel(DMSel), .D_write(Exam_MemData), .A(Exam_MemAddr),
    .D_read(dm_1_d_read));

  // Other names for the same wires on the sheet: DMWE = Exam_MemWrite; GRFWE = Exam_RegWrite; RESET = Input

  // Notes on the sheet:
  //   Outputs
endmodule

module IFU (
  input  [15:0] offset,
  input  clk,
  input  [25:0] instr_index,
  input  RESET,
  input  [31:0] instr_register,
  input  BranchComp,
  input  [1:0] NPCSel,
  output [31:0] PC,
  output [31:0] Instr
);

  wire [31:0] ifu_npc_1_npc, subtractor_1_out;

  IFU_PC ifu_pc_1 (.D(ifu_npc_1_npc), .Q(PC), .in_2(clk), .in_3(RESET));
  IFU_NPC ifu_npc_1 (
    .PC(PC), .NPC(ifu_npc_1_npc), .offset(offset), .instr_index(instr_index),
    .instr_register(instr_register), .NPCSel(NPCSel), .BranchComp(BranchComp));
  Subtractor #(.width(32)) subtractor_1 (.a(PC), .b(32'h3000), .out(subtractor_1_out));  // open: bin, bout
  // Probe on ifu_npc_1_npc
  ROM #(.addrWidth(12), .dataWidth(32)) rom_1 (.addr(subtractor_1_out[13:2]), .data(Instr));  // open: sel

  // Notes on the sheet:
  //   Inputs
  //   PC
  //   NPC
  //   contents of rom_1 (hex, n*v repeats v):
  //   34211234 3c022345 ac010000 ac020004 8c0b0000 8c0d0004 1000ffff
endmodule

module IFU_PC (
  input  [31:0] D,
  input  in_2,
  input  in_3,
  output [31:0] Q
);

  D_Flip_Flop d_ff_1 (.clk(in_2), .D(D[31]), .Q(Q[31]), .en(1'b1), .reset(in_3));  // open: Qn, preset
  D_Flip_Flop d_ff_2 (.clk(in_2), .D(D[30]), .Q(Q[30]), .en(1'b1), .reset(in_3));  // open: Qn, preset
  D_Flip_Flop d_ff_3 (.clk(in_2), .D(D[29]), .Q(Q[29]), .en(1'b1), .reset(in_3));  // open: Qn, preset
  D_Flip_Flop d_ff_4 (.clk(in_2), .D(D[28]), .Q(Q[28]), .en(1'b1), .reset(in_3));  // open: Qn, preset
  D_Flip_Flop d_ff_5 (.clk(in_2), .D(D[27]), .Q(Q[27]), .en(1'b1), .reset(in_3));  // open: Qn, preset
  D_Flip_Flop d_ff_6 (.clk(in_2), .D(D[26]), .Q(Q[26]), .en(1'b1), .reset(in_3));  // open: Qn, preset
  D_Flip_Flop d_ff_7 (.clk(in_2), .D(D[25]), .Q(Q[25]), .en(1'b1), .reset(in_3));  // open: Qn, preset
  D_Flip_Flop d_ff_8 (.clk(in_2), .D(D[24]), .Q(Q[24]), .en(1'b1), .reset(in_3));  // open: Qn, preset
  D_Flip_Flop d_ff_9 (.clk(in_2), .D(D[23]), .Q(Q[23]), .en(1'b1), .reset(in_3));  // open: Qn, preset
  D_Flip_Flop d_ff_10 (.clk(in_2), .D(D[22]), .Q(Q[22]), .en(1'b1), .reset(in_3));  // open: Qn, preset
  D_Flip_Flop d_ff_11 (.clk(in_2), .D(D[21]), .Q(Q[21]), .en(1'b1), .reset(in_3));  // open: Qn, preset
  D_Flip_Flop d_ff_12 (.clk(in_2), .D(D[20]), .Q(Q[20]), .en(1'b1), .reset(in_3));  // open: Qn, preset
  D_Flip_Flop d_ff_13 (.clk(in_2), .D(D[19]), .Q(Q[19]), .en(1'b1), .reset(in_3));  // open: Qn, preset
  D_Flip_Flop d_ff_14 (.clk(in_2), .D(D[18]), .Q(Q[18]), .en(1'b1), .reset(in_3));  // open: Qn, preset
  D_Flip_Flop d_ff_15 (.clk(in_2), .D(D[17]), .Q(Q[17]), .en(1'b1), .reset(in_3));  // open: Qn, preset
  D_Flip_Flop d_ff_16 (.clk(in_2), .D(D[16]), .Q(Q[16]), .en(1'b1), .reset(in_3));  // open: Qn, preset
  D_Flip_Flop d_ff_17 (.clk(in_2), .D(D[15]), .Q(Q[15]), .en(1'b1), .reset(in_3));  // open: Qn, preset
  D_Flip_Flop d_ff_18 (.clk(in_2), .D(D[14]), .Q(Q[14]), .en(1'b1), .reset(in_3));  // open: Qn, preset
  D_Flip_Flop d_ff_19 (.clk(in_2), .D(D[13]), .Q(Q[13]), .preset(in_3), .en(1'b1));  // open: Qn, reset
  D_Flip_Flop d_ff_20 (.clk(in_2), .D(D[12]), .Q(Q[12]), .preset(in_3), .en(1'b1));  // open: Qn, reset
  D_Flip_Flop d_ff_21 (.clk(in_2), .D(D[11]), .Q(Q[11]), .en(1'b1), .reset(in_3));  // open: Qn, preset
  D_Flip_Flop d_ff_22 (.clk(in_2), .D(D[10]), .Q(Q[10]), .en(1'b1), .reset(in_3));  // open: Qn, preset
  D_Flip_Flop d_ff_23 (.clk(in_2), .D(D[9]), .Q(Q[9]), .en(1'b1), .reset(in_3));  // open: Qn, preset
  D_Flip_Flop d_ff_24 (.clk(in_2), .D(D[8]), .Q(Q[8]), .en(1'b1), .reset(in_3));  // open: Qn, preset
  D_Flip_Flop d_ff_25 (.clk(in_2), .D(D[7]), .Q(Q[7]), .en(1'b1), .reset(in_3));  // open: Qn, preset
  D_Flip_Flop d_ff_26 (.clk(in_2), .D(D[6]), .Q(Q[6]), .en(1'b1), .reset(in_3));  // open: Qn, preset
  D_Flip_Flop d_ff_27 (.clk(in_2), .D(D[5]), .Q(Q[5]), .en(1'b1), .reset(in_3));  // open: Qn, preset
  D_Flip_Flop d_ff_28 (.clk(in_2), .D(D[4]), .Q(Q[4]), .en(1'b1), .reset(in_3));  // open: Qn, preset
  D_Flip_Flop d_ff_29 (.clk(in_2), .D(D[3]), .Q(Q[3]), .en(1'b1), .reset(in_3));  // open: Qn, preset
  D_Flip_Flop d_ff_30 (.clk(in_2), .D(D[2]), .Q(Q[2]), .en(1'b1), .reset(in_3));  // open: Qn, preset
  D_Flip_Flop d_ff_31 (.clk(in_2), .D(D[1]), .Q(Q[1]), .en(1'b1), .reset(in_3));  // open: Qn, preset
  D_Flip_Flop d_ff_32 (.clk(in_2), .D(D[0]), .Q(Q[0]), .en(1'b1), .reset(in_3));  // open: Qn, preset

  // Other names for the same wires on the sheet: clk = in_2; reset = in_3

  // Notes on the sheet:
  //   Bit 31-24 (00)
  //   Bit 23-16 (00)
  //   Bit 15-8 (30)
  //   Bit 13
  //   Default=1
  //   Bit 12
  //   Default=1
  //   Bit 7-0 (00)
endmodule

module IFU_NPC (
  input  [31:0] PC,
  input  [15:0] offset,
  input  [25:0] instr_index,
  input  [31:0] instr_register,
  input  BranchComp,
  input  [1:0] NPCSel,
  output [31:0] NPC
);

  wire [31:0] adder_1_out, adder_2_out, bit_extender_1_out, multiplexer_1_out;

  assign bit_extender_1_out = {{14{offset[15]}}, {offset, 2'b00}};  // Bit_Extender bit_extender_1
  Adder #(.width(32)) adder_1 (.a(PC), .b(32'h4), .out(adder_1_out));  // open: cin, cout
  Adder #(.width(32)) adder_2 (.a(adder_1_out), .b(bit_extender_1_out), .out(adder_2_out));  // open: cin, cout
  Multiplexer #(.width(32), .enable("false")) multiplexer_1 (
    .in0(adder_1_out), .in1(adder_2_out), .out(multiplexer_1_out), .sel(BranchComp));
  Multiplexer #(.select(2), .width(32), .enable("false")) multiplexer_2 (
    .in0(adder_1_out), .in1(multiplexer_1_out), .in2({PC[31:28], instr_index, 2'b00}), .in3(instr_register),
    .out(NPC), .sel(NPCSel));

  // Notes on the sheet:
  //   Inputs
endmodule

module SPL (
  input  [31:0] Instr,
  output [5:0] funct,
  output [4:0] shamt,
  output [4:0] rd,
  output [4:0] rt,
  output [4:0] rs,
  output [5:0] opcode,
  output [15:0] imm16,
  output [25:0] instr_index
);


  assign funct = Instr[5:0];
  assign imm16 = Instr[15:0];
  assign instr_index = Instr[25:0];
  assign opcode = Instr[31:26];
  assign rd = Instr[15:11];
  assign rs = Instr[25:21];
  assign rt = Instr[20:16];
  assign shamt = Instr[10:6];

  // Notes on the sheet:
  //   Input
  //   Outputs
endmodule

module GRF (
  input  clk,
  input  reset,
  input  WE,
  input  [4:0] A1,
  input  [4:0] A2,
  input  [4:0] A3,
  input  [31:0] WD,
  output [31:0] RD1,
  output [31:0] RD2
);

  wire E00, E01, E02, E03, E04, E05, E06, E07, E08, E09, E10, E11, E12, E13, E14, E15, E16, E17, E18, E19,
       E20, E21, E22, E23, E24, E25, E26, E27, E28, E29, E30, E31;
  wire [31:0] O01, O02, O03, O04, O05, O06, O07, O08, O09, O10, O11, O12, O13, O14, O15, O16, O17, O18, O19,
       O20, O21, O22, O23, O24, O25, O26, O27, O28, O29, O30, O31;

  Register #(.width(32)) register_1 (.D(WD), .en(E08), .Q(O08), .clk(clk), .clr(reset));
  Register #(.width(32)) register_2 (.D(WD), .en(E16), .Q(O16), .clk(clk), .clr(reset));
  Register #(.width(32)) register_3 (.D(WD), .en(E24), .Q(O24), .clk(clk), .clr(reset));
  Register #(.width(32)) register_4 (.D(WD), .en(E01), .Q(O01), .clk(clk), .clr(reset));
  Register #(.width(32)) register_5 (.D(WD), .en(E09), .Q(O09), .clk(clk), .clr(reset));
  Register #(.width(32)) register_6 (.D(WD), .en(E17), .Q(O17), .clk(clk), .clr(reset));
  Register #(.width(32)) register_7 (.D(WD), .en(E25), .Q(O25), .clk(clk), .clr(reset));
  Register #(.width(32)) register_8 (.D(WD), .en(E02), .Q(O02), .clk(clk), .clr(reset));
  Register #(.width(32)) register_9 (.D(WD), .en(E10), .Q(O10), .clk(clk), .clr(reset));
  Register #(.width(32)) register_10 (.D(WD), .en(E18), .Q(O18), .clk(clk), .clr(reset));
  Register #(.width(32)) register_11 (.D(WD), .en(E26), .Q(O26), .clk(clk), .clr(reset));
  Multiplexer #(.select(5), .width(32), .enable("false")) multiplexer_1 (
    .in0({32{1'b0}}), .in1(O01), .in2(O02), .in3(O03), .in4(O04), .in5(O05), .in6(O06), .in7(O07), .in8(O08),
    .in9(O09), .in10(O10), .in11(O11), .in12(O12), .in13(O13), .in14(O14), .in15(O15), .in16(O16),
    .in17(O17), .in18(O18), .in19(O19), .in20(O20), .in21(O21), .in22(O22), .in23(O23), .in24(O24),
    .in25(O25), .in26(O26), .in27(O27), .in28(O28), .in29(O29), .in30(O30), .in31(O31), .out(RD1), .sel(A1));
  Register #(.width(32)) register_12 (.D(WD), .en(E03), .Q(O03), .clk(clk), .clr(reset));
  Register #(.width(32)) register_13 (.D(WD), .en(E11), .Q(O11), .clk(clk), .clr(reset));
  Register #(.width(32)) register_14 (.D(WD), .en(E19), .Q(O19), .clk(clk), .clr(reset));
  Register #(.width(32)) register_15 (.D(WD), .en(E27), .Q(O27), .clk(clk), .clr(reset));
  Register #(.width(32)) register_16 (.D(WD), .en(E04), .Q(O04), .clk(clk), .clr(reset));
  Register #(.width(32)) register_17 (.D(WD), .en(E12), .Q(O12), .clk(clk), .clr(reset));
  Register #(.width(32)) register_18 (.D(WD), .en(E20), .Q(O20), .clk(clk), .clr(reset));
  Register #(.width(32)) register_19 (.D(WD), .en(E28), .Q(O28), .clk(clk), .clr(reset));
  Multiplexer #(.select(5), .width(32), .enable("false")) multiplexer_2 (
    .in0({32{1'b0}}), .in1(O01), .in2(O02), .in3(O03), .in4(O04), .in5(O05), .in6(O06), .in7(O07), .in8(O08),
    .in9(O09), .in10(O10), .in11(O11), .in12(O12), .in13(O13), .in14(O14), .in15(O15), .in16(O16),
    .in17(O17), .in18(O18), .in19(O19), .in20(O20), .in21(O21), .in22(O22), .in23(O23), .in24(O24),
    .in25(O25), .in26(O26), .in27(O27), .in28(O28), .in29(O29), .in30(O30), .in31(O31), .out(RD2), .sel(A2));
  Register #(.width(32)) register_20 (.D(WD), .en(E05), .Q(O05), .clk(clk), .clr(reset));
  Register #(.width(32)) register_21 (.D(WD), .en(E13), .Q(O13), .clk(clk), .clr(reset));
  Register #(.width(32)) register_22 (.D(WD), .en(E21), .Q(O21), .clk(clk), .clr(reset));
  Register #(.width(32)) register_23 (.D(WD), .en(E29), .Q(O29), .clk(clk), .clr(reset));
  Decoder #(.select(5), .disabled(0)) decoder_1 (
    .out0(E00), .out1(E01), .out2(E02), .out3(E03), .out4(E04), .out5(E05), .out6(E06), .out7(E07),
    .out8(E08), .out9(E09), .out10(E10), .out11(E11), .out12(E12), .out13(E13), .out14(E14), .out15(E15),
    .out16(E16), .out17(E17), .out18(E18), .out19(E19), .out20(E20), .out21(E21), .out22(E22), .out23(E23),
    .out24(E24), .out25(E25), .out26(E26), .out27(E27), .out28(E28), .out29(E29), .out30(E30), .out31(E31),
    .sel(A3), .en(WE));
  Register #(.width(32)) register_24 (.D(WD), .en(E06), .Q(O06), .clk(clk), .clr(reset));
  Register #(.width(32)) register_25 (.D(WD), .en(E14), .Q(O14), .clk(clk), .clr(reset));
  Register #(.width(32)) register_26 (.D(WD), .en(E22), .Q(O22), .clk(clk), .clr(reset));
  Register #(.width(32)) register_27 (.D(WD), .en(E30), .Q(O30), .clk(clk), .clr(reset));
  Register #(.width(32)) register_28 (.D(WD), .en(E07), .Q(O07), .clk(clk), .clr(reset));
  Register #(.width(32)) register_29 (.D(WD), .en(E15), .Q(O15), .clk(clk), .clr(reset));
  Register #(.width(32)) register_30 (.D(WD), .en(E23), .Q(O23), .clk(clk), .clr(reset));
  Register #(.width(32)) register_31 (.D(WD), .en(E31), .Q(O31), .clk(clk), .clr(reset));

  // Notes on the sheet:
  //   Inputs
  //   Outputs
endmodule

module ALU (
  input  [31:0] rs,
  input  [31:0] rt,
  input  [4:0] shamt,
  input  [1:0] OPSel,
  input  [2:0] FuncSel,
  input  [2:0] CompSel,
  output [31:0] OP,
  output Comp
);

  wire not_1_out, or_1_out, or_2_out, seq, sgt, slt, ueq, ugt, ult, xnor_1_out;
  wire [4:0] multiplexer_2_out;
  wire [31:0] adder_1_out, and_1_out, bit_extender_1_out, multiplexer_1_out, multiplexer_3_out,
       multiplexer_5_out, multiplexer_6_out, not_2_out, not_3_out, or_3_out, shifter_1_out, shifter_2_out,
       shifter_3_out, xor_1_out;

  Multiplexer #(.width(32), .enable("false")) multiplexer_1 (
    .in0(rt), .in1({32{1'b0}}), .out(multiplexer_1_out), .sel(xnor_1_out));
  xnor xnor_1 (xnor_1_out, CompSel[2], CompSel[1]);
  Comparator #(.width(32), .mode("unsigned")) comparator_1 (.a(rs), .b(rt), .gt(ult), .eq(ueq), .lt(ugt));
  Comparator #(.width(32)) comparator_2 (.a(rs), .b(multiplexer_1_out), .gt(slt), .eq(seq), .lt(sgt));
  Multiplexer #(.width(5), .enable("false")) multiplexer_2 (
    .in0(shamt), .in1(rt[4:0]), .out(multiplexer_2_out), .sel(FuncSel[2]));
  or or_1 (or_1_out, sgt, seq);
  not not_1 (not_1_out, ueq);
  or or_2 (or_2_out, slt, seq);
  assign not_2_out = ~rt;  // NOT_Gate not_2, 32 bits wide
  assign and_1_out = rs & rt;  // AND_Gate and_1, 32 bits wide
  assign or_3_out = rs | rt;  // OR_Gate or_3, 32 bits wide
  assign xor_1_out = rs ^ rt;  // XOR_Gate xor_1, 32 bits wide
  Multiplexer #(.width(32), .enable("false")) multiplexer_3 (
    .in0(rt), .in1(not_2_out), .out(multiplexer_3_out), .sel(FuncSel[0]));
  assign not_3_out = ~or_3_out;  // NOT_Gate not_3, 32 bits wide
  Shifter #(.width(32)) shifter_1 (.in(rs), .\dist (multiplexer_2_out), .out(shifter_1_out));
  Shifter #(.width(32), .shift("lr")) shifter_2 (.in(rs), .\dist (multiplexer_2_out), .out(shifter_2_out));
  Shifter #(.width(32), .shift("ar")) shifter_3 (.in(rs), .\dist (multiplexer_2_out), .out(shifter_3_out));
  Multiplexer #(.select(3), .enable("false")) multiplexer_4 (
    .in0(slt), .in1(or_1_out), .in2(slt), .in3(ult), .in4(ueq), .in5(not_1_out), .in6(or_2_out), .in7(sgt),
    .out(Comp), .sel(CompSel));
  Adder #(.width(32)) adder_1 (.a(rs), .b(multiplexer_3_out), .out(adder_1_out), .cin(FuncSel[0]));  // open: cout
  Multiplexer #(.select(2), .width(32), .enable("false")) multiplexer_5 (
    .in0(and_1_out), .in1(or_3_out), .in2(xor_1_out), .in3(not_3_out), .out(multiplexer_5_out),
    .sel(FuncSel[1:0]));
  Multiplexer #(.select(2), .width(32), .enable("false")) multiplexer_6 (
    .in0(shifter_1_out), .in1(shifter_1_out), .in2(shifter_2_out), .in3(shifter_3_out),
    .out(multiplexer_6_out), .sel(FuncSel[1:0]));
  assign bit_extender_1_out = {{31{1'b0}}, Comp};  // Bit_Extender bit_extender_1
  Multiplexer #(.select(2), .width(32), .enable("false")) multiplexer_7 (
    .in0(adder_1_out), .in1(multiplexer_5_out), .in2(multiplexer_6_out), .in3(bit_extender_1_out), .out(OP),
    .sel(OPSel));

  // Notes on the sheet:
  //   Inputs
  //   Compare
  //   Arithmetic
  //   Logical
  //   Shift
endmodule

module EXT (
  input  [15:0] imm16,
  input  [1:0] in_2,
  output [31:0] EXT
);

  wire [31:0] bit_extender_1_out, bit_extender_2_out;

  assign bit_extender_1_out = {{16{imm16[15]}}, imm16};  // Bit_Extender bit_extender_1
  assign bit_extender_2_out = {{16{1'b0}}, imm16};  // Bit_Extender bit_extender_2
  Multiplexer #(.select(2), .width(32), .enable("false")) multiplexer_1 (
    .in0(bit_extender_1_out), .in1(bit_extender_2_out), .in2({imm16, {16{1'b0}}}), .in3({imm16, {16{1'b0}}}),
    .out(EXT), .sel(in_2));

  // Other names for the same wires on the sheet: EXTSel[1:0] = in_2

  // Notes on the sheet:
  //   Inputs
endmodule

module DM (
  input  clk,
  input  RESET,
  input  WE,
  input  [2:0] DMSel,
  input  [31:0] A,
  input  [31:0] D_write,
  output [31:0] D_read
);

  wire [7:0] multiplexer_4_out, undriven;
  wire [15:0] multiplexer_5_out;
  wire [31:0] bit_extender_1_out, bit_extender_2_out, bit_extender_3_out, bit_extender_4_out,
       multiplexer_1_out, multiplexer_2_out, multiplexer_6_out, multiplexer_7_out, RAM_D_read, RAM_D_write;

  RAM #(.addrWidth(12), .dataWidth(32), .bus("separate")) ram_1 (
    .addr(A[13:2]), .din(RAM_D_write), .data(RAM_D_read), .str(WE), .sel(1'b1), .clk(clk), .ld(1'b1),
    .clr(RESET));
  Multiplexer #(.select(2), .width(32), .enable("false")) multiplexer_1 (
    .in0({RAM_D_read[31:8], D_write[7:0]}), .in1({RAM_D_read[31:16], D_write[7:0], RAM_D_read[7:0]}),
    .in2({RAM_D_read[31:24], D_write[7:0], RAM_D_read[15:0]}), .in3({undriven, RAM_D_read[23:0]}),
    .out(multiplexer_1_out), .sel(A[1:0]));
  Multiplexer #(.width(32), .enable("false")) multiplexer_2 (
    .in0({RAM_D_read[31:16], D_write[15:0]}), .in1({D_write[15:0], RAM_D_read[15:0]}),
    .out(multiplexer_2_out), .sel(A[1]));
  Multiplexer #(.select(2), .width(32), .enable("false")) multiplexer_3 (
    .in0(multiplexer_1_out), .in1(multiplexer_2_out), .in2(D_write), .in3(D_write), .out(RAM_D_write),
    .sel(DMSel[1:0]));
  Multiplexer #(.select(2), .width(8), .enable("false")) multiplexer_4 (
    .in0(RAM_D_read[7:0]), .in1(RAM_D_read[15:8]), .in2(RAM_D_read[23:16]), .in3(RAM_D_read[31:24]),
    .out(multiplexer_4_out), .sel(A[1:0]));
  Multiplexer #(.width(16), .enable("false")) multiplexer_5 (
    .in0(RAM_D_read[15:0]), .in1(RAM_D_read[31:16]), .out(multiplexer_5_out), .sel(A[1]));
  assign bit_extender_1_out = {{24{multiplexer_4_out[7]}}, multiplexer_4_out};  // Bit_Extender bit_extender_1
  assign bit_extender_2_out = {{24{1'b0}}, multiplexer_4_out};  // Bit_Extender bit_extender_2
  assign bit_extender_3_out = {{16{multiplexer_5_out[15]}}, multiplexer_5_out};  // Bit_Extender bit_extender_3
  assign bit_extender_4_out = {{16{1'b0}}, multiplexer_5_out};  // Bit_Extender bit_extender_4
  Multiplexer #(.width(32), .enable("false")) multiplexer_6 (
    .in0(bit_extender_1_out), .in1(bit_extender_2_out), .out(multiplexer_6_out), .sel(DMSel[2]));
  Multiplexer #(.width(32), .enable("false")) multiplexer_7 (
    .in0(bit_extender_3_out), .in1(bit_extender_4_out), .out(multiplexer_7_out), .sel(DMSel[2]));
  Multiplexer #(.select(2), .width(32), .enable("false")) multiplexer_8 (
    .in0(multiplexer_6_out), .in1(multiplexer_7_out), .in2(RAM_D_read), .in3(RAM_D_read), .out(D_read),
    .sel(DMSel[1:0]));

  // Other names for the same wires on the sheet: D_write_byte[7:0] = D_write[7:0]; D_write_half[15:0] = D_write[15:0];
  //   D_write_word[31:0] = D_write; A_byte[1:0] = A[1:0]; RAM_addr[11:0] = A[13:2]

  // Notes on the sheet:
  //   Inputs
  //   RAM
  //   Handle D_write
  //   Handle D_read
endmodule

module CTRL (
  input  [5:0] opcode,
  input  [5:0] funct,
  input  [4:0] rt,
  output [1:0] OPSel,
  output [1:0] EXTSel,
  output [2:0] DMSel,
  output [1:0] NPCSel,
  output [2:0] FuncSel,
  output [2:0] CompSel,
  output GRFWE,
  output DMWE,
  output [1:0] GRFA3MUX,
  output [1:0] GRFWDMUX,
  output ALUrtMUX
);

  wire ctrl_and_1_addiu, ctrl_and_1_addu, ctrl_and_1_and, ctrl_and_1_andi, ctrl_and_1_beq, ctrl_and_1_bgez,
       ctrl_and_1_bgtz, ctrl_and_1_blez, ctrl_and_1_bltz, ctrl_and_1_bne, ctrl_and_1_ij, ctrl_and_1_j,
       ctrl_and_1_jal, ctrl_and_1_jalr, ctrl_and_1_jr, ctrl_and_1_lb, ctrl_and_1_lbu, ctrl_and_1_lh,
       ctrl_and_1_lhu, ctrl_and_1_lui, ctrl_and_1_lw, ctrl_and_1_nor, ctrl_and_1_or, ctrl_and_1_ori,
       ctrl_and_1_r, ctrl_and_1_sb, ctrl_and_1_sh, ctrl_and_1_sll, ctrl_and_1_sllv, ctrl_and_1_slt,
       ctrl_and_1_slti, ctrl_and_1_sltiu, ctrl_and_1_sltu, ctrl_and_1_sra, ctrl_and_1_srav, ctrl_and_1_srl,
       ctrl_and_1_srlv, ctrl_and_1_subu, ctrl_and_1_sw, ctrl_and_1_xor, ctrl_and_1_xori;

  CTRL_AND ctrl_and_1 (
    .opcode(opcode), .funct(funct), .rt(rt), .addu(ctrl_and_1_addu), .subu(ctrl_and_1_subu),
    .ori(ctrl_and_1_ori), .lui(ctrl_and_1_lui), .lb(ctrl_and_1_lb), .sw(ctrl_and_1_sw),
    .addiu(ctrl_and_1_addiu), .\and (ctrl_and_1_and), .\or (ctrl_and_1_or), .\xor (ctrl_and_1_xor),
    .\nor (ctrl_and_1_nor), .sll(ctrl_and_1_sll), .srl(ctrl_and_1_srl), .sllv(ctrl_and_1_sllv),
    .srlv(ctrl_and_1_srlv), .sra(ctrl_and_1_sra), .srav(ctrl_and_1_srav), .andi(ctrl_and_1_andi),
    .xori(ctrl_and_1_xori), .slt(ctrl_and_1_slt), .sltu(ctrl_and_1_sltu), .slti(ctrl_and_1_slti),
    .sltiu(ctrl_and_1_sltiu), .lh(ctrl_and_1_lh), .lw(ctrl_and_1_lw), .lbu(ctrl_and_1_lbu),
    .sb(ctrl_and_1_sb), .sh(ctrl_and_1_sh), .lhu(ctrl_and_1_lhu), .bne(ctrl_and_1_bne),
    .blez(ctrl_and_1_blez), .bgtz(ctrl_and_1_bgtz), .bltz(ctrl_and_1_bltz), .bgez(ctrl_and_1_bgez),
    .jr(ctrl_and_1_jr), .jalr(ctrl_and_1_jalr), .j(ctrl_and_1_j), .jal(ctrl_and_1_jal), .beq(ctrl_and_1_beq),
    .R(ctrl_and_1_r), .IJ(ctrl_and_1_ij));
  CTRL_OR ctrl_or_1 (
    .OPSel(OPSel), .EXTSel(EXTSel), .DMSel(DMSel), .NPCSel(NPCSel), .FuncSel(FuncSel), .CompSel(CompSel),
    .GRFWE(GRFWE), .DMWE(DMWE), .opcode(opcode), .funct(funct), .rt(rt), .GRFA3MUX(GRFA3MUX),
    .GRFWDMUX(GRFWDMUX), .ALUrtMUX(ALUrtMUX), .addu(ctrl_and_1_addu), .subu(ctrl_and_1_subu),
    .addiu(ctrl_and_1_addiu), .\and (ctrl_and_1_and), .\or (ctrl_and_1_or), .\xor (ctrl_and_1_xor),
    .\nor (ctrl_and_1_nor), .sll(ctrl_and_1_sll), .srl(ctrl_and_1_srl), .sra(ctrl_and_1_sra),
    .sllv(ctrl_and_1_sllv), .srlv(ctrl_and_1_srlv), .srav(ctrl_and_1_srav), .slt(ctrl_and_1_slt),
    .sltu(ctrl_and_1_sltu), .lui(ctrl_and_1_lui), .slti(ctrl_and_1_slti), .sltiu(ctrl_and_1_sltiu),
    .lb(ctrl_and_1_lb), .lh(ctrl_and_1_lh), .lw(ctrl_and_1_lw), .lbu(ctrl_and_1_lbu), .lhu(ctrl_and_1_lhu),
    .sb(ctrl_and_1_sb), .sh(ctrl_and_1_sh), .sw(ctrl_and_1_sw), .beq(ctrl_and_1_beq), .bne(ctrl_and_1_bne),
    .blez(ctrl_and_1_blez), .bgtz(ctrl_and_1_bgtz), .bltz(ctrl_and_1_bltz), .bgez(ctrl_and_1_bgez),
    .jr(ctrl_and_1_jr), .jalr(ctrl_and_1_jalr), .j(ctrl_and_1_j), .jal(ctrl_and_1_jal),
    .andi(ctrl_and_1_andi), .ori(ctrl_and_1_ori), .xori(ctrl_and_1_xori), .R(ctrl_and_1_r), .IJ(ctrl_and_1_ij));

  // Notes on the sheet:
  //   Inputs
  //   Outputs
endmodule

module CTRL_AND (
  input  [5:0] opcode,
  input  [5:0] funct,
  input  [4:0] rt,
  output R,
  output IJ,
  output slt,
  output addu,
  output sltu,
  output beq,
  output bne,
  output subu,
  output lui,
  output blez,
  output slti,
  output bgtz,
  output sltiu,
  output addiu,
  output bltz,
  output lb,
  output bgez,
  output \and ,
  output lh,
  output \or ,
  output lw,
  output jr,
  output \xor ,
  output lbu,
  output jalr,
  output \nor ,
  output lhu,
  output sll,
  output sb,
  output j,
  output srl,
  output sh,
  output jal,
  output sra,
  output sw,
  output sllv,
  output srlv,
  output srav,
  output andi,
  output ori,
  output xori
);

  wire funct_add, funct_addu, funct_and, funct_jalr, funct_jr, funct_nor, funct_or, funct_sll, funct_sllv,
       funct_slt, funct_sltu, funct_sra, funct_srav, funct_srl, funct_srlv, funct_sub, funct_subu, funct_xor,
       not_1_out, not_2_out, not_3_out, not_4_out, not_5_out, not_6_out, not_7_out, not_8_out, not_9_out,
       not_10_out, not_11_out, not_12_out, not_13_out, not_14_out, not_15_out, not_16_out, not_17_out,
       not_18_out, not_19_out, not_20_out, not_21_out, not_22_out, not_23_out, not_24_out, not_26_out,
       not_27_out, not_28_out, not_29_out, not_30_out, not_31_out, not_32_out, not_33_out, not_34_out,
       not_35_out, not_36_out, not_37_out, not_38_out, not_39_out, not_40_out, not_41_out, not_42_out,
       not_43_out, not_44_out, not_45_out, not_46_out, not_47_out, not_48_out, not_49_out, not_50_out,
       not_51_out, not_52_out, not_53_out, not_54_out, not_55_out, not_56_out, not_57_out, not_58_out,
       not_59_out, not_60_out, not_61_out, not_62_out, not_63_out, not_64_out, not_65_out, not_66_out,
       not_67_out, not_68_out, not_69_out, not_70_out, not_71_out, not_72_out, not_73_out, not_74_out,
       not_75_out, not_76_out, not_77_out, not_78_out, opcode_addiu, opcode_andi, opcode_beq, opcode_bgtz,
       opcode_blez, opcode_bne, opcode_j, opcode_jal, opcode_lb, opcode_lbu, opcode_lh, opcode_lhu,
       opcode_lui, opcode_lw, opcode_ori, opcode_regimm, opcode_sb, opcode_sh, opcode_slti, opcode_sltiu,
       opcode_sw, opcode_xori, or_1_out, or_2_out, rt_bgez, rt_bltz;

  not not_1 (not_1_out, funct[4]);
  not not_2 (not_2_out, funct[2]);
  not not_3 (not_3_out, funct[0]);
  not not_4 (not_4_out, funct[1]);
  not not_5 (not_5_out, funct[3]);
  not not_6 (not_6_out, funct[5]);
  not not_7 (not_7_out, opcode[5]);
  not not_8 (not_8_out, opcode[1]);
  not not_9 (not_9_out, opcode[2]);
  not not_10 (not_10_out, opcode[0]);
  not not_11 (not_11_out, opcode[3]);
  not not_12 (not_12_out, opcode[4]);
  not not_13 (not_13_out, funct[3]);
  not not_14 (not_14_out, funct[0]);
  not not_15 (not_15_out, funct[5]);
  not not_16 (not_16_out, funct[1]);
  not not_17 (not_17_out, funct[4]);
  not not_18 (not_18_out, funct[2]);
  not not_19 (not_19_out, opcode[2]);
  not not_20 (not_20_out, opcode[1]);
  not not_21 (not_21_out, opcode[0]);
  not not_22 (not_22_out, opcode[4]);
  not not_23 (not_23_out, opcode[5]);
  not not_24 (not_24_out, opcode[3]);
  and and_1 (funct_add, funct[5], not_1_out, not_5_out, not_2_out, not_4_out, not_3_out);
  and and_2 (funct_addu, funct[5], not_1_out, not_5_out, not_2_out, not_4_out, funct[0]);
  and and_3 (funct_sub, funct[5], not_1_out, not_5_out, not_2_out, funct[1], not_3_out);
  and and_4 (funct_subu, funct[5], not_1_out, not_5_out, not_2_out, funct[1], funct[0]);
  and and_5 (opcode_addiu, not_7_out, not_12_out, opcode[3], not_9_out, not_8_out, opcode[0]);
  and and_6 (funct_and, funct[5], not_17_out, not_13_out, funct[2], not_16_out, not_14_out);
  and and_7 (funct_or, funct[5], not_17_out, not_13_out, funct[2], not_16_out, funct[0]);
  and and_8 (funct_xor, funct[5], not_17_out, not_13_out, funct[2], funct[1], not_14_out);
  and and_9 (funct_nor, funct[5], not_17_out, not_13_out, funct[2], funct[1], funct[0]);
  and and_10 (funct_sll, not_15_out, not_17_out, not_13_out, not_18_out, not_16_out, not_14_out);
  and and_11 (funct_srl, not_15_out, not_17_out, not_13_out, not_18_out, funct[1], not_14_out);
  and and_12 (funct_sra, not_15_out, not_17_out, not_13_out, not_18_out, funct[1], funct[0]);
  and and_13 (funct_sllv, not_15_out, not_17_out, not_13_out, funct[2], not_16_out, not_14_out);
  and and_14 (funct_srlv, not_15_out, not_17_out, not_13_out, funct[2], funct[1], not_14_out);
  and and_15 (funct_srav, not_15_out, not_17_out, not_18_out, funct[2], funct[1], funct[0]);
  and and_16 (opcode_andi, not_23_out, not_22_out, opcode[3], opcode[2], not_20_out, not_21_out);
  and and_17 (opcode_ori, not_23_out, not_22_out, opcode[3], opcode[2], not_20_out, opcode[0]);
  and and_18 (opcode_xori, not_23_out, not_22_out, opcode[3], opcode[2], opcode[1], not_21_out);
  nor nor_1 (R, opcode[0], opcode[1], opcode[2], opcode[3], opcode[4], opcode[5]);
  not not_25 (IJ, R);
  or or_1 (or_1_out, funct_add, funct_addu);
  or or_2 (or_2_out, funct_sub, funct_subu);
  and and_19 (addu, R, or_1_out);
  and and_20 (subu, R, or_2_out);
  and and_21 (addiu, IJ, opcode_addiu);
  and and_22 (\and , R, funct_and);
  and and_23 (\or , R, funct_or);
  and and_24 (\xor , R, funct_xor);
  and and_25 (\nor , R, funct_nor);
  and and_26 (sll, R, funct_sll);
  and and_27 (srl, R, funct_srl);
  and and_28 (sra, R, funct_sra);
  and and_29 (sllv, R, funct_sllv);
  and and_30 (srlv, R, funct_srlv);
  and and_31 (srav, R, funct_srav);
  and and_32 (andi, IJ, opcode_andi);
  and and_33 (ori, IJ, opcode_ori);
  and and_34 (xori, IJ, opcode_xori);
  not not_26 (not_26_out, funct[3]);
  not not_27 (not_27_out, funct[1]);
  not not_28 (not_28_out, funct[5]);
  not not_29 (not_29_out, funct[4]);
  not not_30 (not_30_out, funct[2]);
  not not_31 (not_31_out, funct[0]);
  not not_32 (not_32_out, opcode[5]);
  not not_33 (not_33_out, opcode[3]);
  not not_34 (not_34_out, opcode[1]);
  not not_35 (not_35_out, opcode[0]);
  not not_36 (not_36_out, opcode[2]);
  not not_37 (not_37_out, opcode[4]);
  not not_38 (not_38_out, opcode[4]);
  not not_39 (not_39_out, opcode[2]);
  not not_40 (not_40_out, opcode[1]);
  not not_41 (not_41_out, opcode[3]);
  not not_42 (not_42_out, opcode[5]);
  not not_43 (not_43_out, opcode[0]);
  and and_35 (funct_slt, funct[5], not_29_out, funct[3], not_30_out, funct[1], not_31_out);
  and and_36 (funct_sltu, funct[5], not_29_out, funct[3], not_30_out, funct[1], funct[0]);
  and and_37 (opcode_lui, not_32_out, not_37_out, opcode[3], opcode[2], opcode[1], opcode[0]);
  and and_38 (opcode_slti, not_32_out, not_37_out, opcode[3], not_36_out, opcode[1], not_35_out);
  and and_39 (opcode_sltiu, not_32_out, not_37_out, opcode[3], not_36_out, opcode[1], opcode[0]);
  and and_40 (opcode_lb, opcode[5], not_38_out, not_41_out, not_39_out, not_40_out, not_43_out);
  and and_41 (opcode_lh, opcode[5], not_38_out, not_41_out, not_39_out, not_40_out, opcode[0]);
  and and_42 (opcode_lw, opcode[5], not_38_out, not_41_out, not_39_out, opcode[1], opcode[0]);
  and and_43 (opcode_lbu, opcode[5], not_38_out, not_41_out, opcode[2], not_40_out, not_43_out);
  and and_44 (opcode_lhu, opcode[5], not_38_out, not_39_out, opcode[2], not_40_out, opcode[0]);
  and and_45 (opcode_sb, opcode[5], not_38_out, opcode[3], not_39_out, not_40_out, not_43_out);
  and and_46 (opcode_sh, opcode[5], not_38_out, opcode[3], not_39_out, not_40_out, opcode[0]);
  and and_47 (opcode_sw, opcode[5], not_38_out, opcode[3], not_39_out, opcode[1], opcode[0]);
  and and_48 (slt, R, funct_slt);
  and and_49 (sltu, R, funct_sltu);
  and and_50 (lui, IJ, opcode_lui);
  and and_51 (slti, IJ, opcode_slti);
  and and_52 (sltiu, IJ, opcode_sltiu);
  and and_53 (lb, IJ, opcode_lb);
  and and_54 (lh, IJ, opcode_lh);
  and and_55 (lw, IJ, opcode_lw);
  and and_56 (lbu, IJ, opcode_lbu);
  and and_57 (lhu, IJ, opcode_lhu);
  and and_58 (sb, IJ, opcode_sb);
  and and_59 (sh, IJ, opcode_sh);
  and and_60 (sw, IJ, opcode_sw);
  not not_44 (not_44_out, opcode[5]);
  not not_45 (not_45_out, opcode[4]);
  not not_46 (not_46_out, rt[4]);
  not not_47 (not_47_out, funct[4]);
  not not_48 (not_48_out, funct[5]);
  not not_49 (not_49_out, opcode[4]);
  not not_50 (not_50_out, opcode[5]);
  not not_51 (not_51_out, opcode[3]);
  not not_52 (not_52_out, opcode[2]);
  not not_53 (not_53_out, opcode[1]);
  not not_54 (not_54_out, opcode[0]);
  not not_55 (not_55_out, rt[1]);
  not not_56 (not_56_out, rt[3]);
  not not_57 (not_57_out, rt[2]);
  not not_58 (not_58_out, rt[0]);
  not not_59 (not_59_out, funct[3]);
  not not_60 (not_60_out, funct[1]);
  not not_61 (not_61_out, funct[2]);
  not not_62 (not_62_out, funct[0]);
  not not_63 (not_63_out, opcode[0]);
  not not_64 (not_64_out, opcode[3]);
  not not_65 (not_65_out, opcode[2]);
  not not_66 (not_66_out, opcode[1]);
  and and_61 (opcode_regimm, not_44_out, not_45_out, not_51_out, not_52_out, not_53_out, opcode[0]);
  and and_62 (opcode_beq, not_44_out, not_45_out, not_51_out, opcode[2], not_53_out, not_54_out);
  and and_63 (opcode_bne, not_44_out, not_45_out, not_51_out, opcode[2], not_53_out, opcode[0]);
  and and_64 (opcode_blez, not_44_out, not_45_out, not_51_out, opcode[2], opcode[1], not_54_out);
  and and_65 (opcode_bgtz, not_44_out, not_45_out, not_51_out, opcode[2], opcode[1], opcode[0]);
  and and_66 (rt_bltz, not_46_out, not_56_out, not_57_out, not_55_out, not_58_out);
  and and_67 (rt_bgez, not_46_out, not_56_out, not_57_out, not_55_out, rt[0]);
  and and_68 (funct_jr, not_48_out, not_47_out, funct[3], not_61_out, not_60_out, not_62_out);
  and and_69 (funct_jalr, not_48_out, not_47_out, funct[3], not_61_out, not_60_out, funct[0]);
  and and_70 (opcode_j, not_50_out, not_49_out, not_64_out, not_65_out, opcode[1], not_63_out);
  and and_71 (opcode_jal, not_50_out, not_49_out, not_64_out, not_65_out, opcode[1], opcode[0]);
  and and_72 (beq, IJ, opcode_beq);
  and and_73 (bne, IJ, opcode_bne);
  and and_74 (blez, IJ, opcode_blez);
  and and_75 (bgtz, IJ, opcode_bgtz);
  and and_76 (bltz, IJ, opcode_regimm, rt_bltz);
  and and_77 (bgez, IJ, opcode_regimm, rt_bgez);
  and and_78 (jr, R, funct_jr);
  and and_79 (jalr, R, funct_jalr);
  and and_80 (j, IJ, opcode_j);
  and and_81 (jal, IJ, opcode_jal);
  not not_67 (not_67_out, funct[4]);
  not not_68 (not_68_out, funct[5]);
  not not_69 (not_69_out, funct[2]);
  not not_70 (not_70_out, funct[3]);
  not not_71 (not_71_out, funct[1]);
  not not_72 (not_72_out, funct[0]);
  not not_73 (not_73_out, opcode[5]);
  not not_74 (not_74_out, opcode[3]);
  not not_75 (not_75_out, opcode[4]);
  not not_76 (not_76_out, opcode[2]);
  not not_77 (not_77_out, opcode[1]);
  not not_78 (not_78_out, opcode[0]);

  // Notes on the sheet:
  //   Inputs
  //   Arithmetic
  //   R
  //   Arithmetic
  //   I
  //   Logical
  //   R
  //   Arithmetic
  //   I
  //   100000
  //   100001
  //   100010
  //   100011
  //   001001
  //   100100
  //   100101
  //   100110
  //   100111
  //   000000
  //   000010
  //   000011
  //   000100
  //   000110
  //   000111
  //   001100
  //   001101
  //   001110
  //   Outputs
  //   Register
  //   R
  //   Register
  //   I
  //   Memory
  //   I
  //   101010
  //   101011
  //   001111
  //   001010
  //   001011
  //   100000
  //   100001
  //   100011
  //   100100
  //   100101
  //   101000
  //   101001
  //   101011
  //   Outputs
  //   Branch
  //   I
  //   Jump
  //   R
  //   Jump
  //   J
  //   000001
  //   000100
  //   000101
  //   000110
  //   000111
  //   00000
  //   00001
  //   001000
  //   001001
  //   000010
  //   000011
  //   Outputs
  //   Additional
  //   R
  //   Outputs
  //   Additional
  //   IJ
  //   Outputs
endmodule

module CTRL_OR (
  input  [5:0] opcode,
  input  R,
  input  [5:0] funct,
  input  IJ,
  input  [4:0] rt,
  input  addu,
  input  subu,
  input  addiu,
  input  \and ,
  input  \or ,
  input  \xor ,
  input  \nor ,
  input  sll,
  input  srl,
  input  sra,
  input  sllv,
  input  srlv,
  input  srav,
  input  andi,
  input  ori,
  input  xori,
  input  slt,
  input  sltu,
  input  lui,
  input  slti,
  input  sltiu,
  input  lb,
  input  lh,
  input  lw,
  input  lbu,
  input  lhu,
  input  sb,
  input  sh,
  input  sw,
  input  beq,
  input  bne,
  input  blez,
  input  bgtz,
  input  bltz,
  input  bgez,
  input  jr,
  input  jalr,
  input  j,
  input  jal,
  output [1:0] GRFA3MUX,
  output [1:0] OPSel,
  output [1:0] GRFWDMUX,
  output [1:0] EXTSel,
  output ALUrtMUX,
  output [2:0] DMSel,
  output [1:0] NPCSel,
  output [2:0] FuncSel,
  output [2:0] CompSel,
  output GRFWE,
  output DMWE
);

  wire and_1_out, nor_1_out, not_1_out, or_1_out, or_2_out, or_3_out, or_4_out, or_5_out, or_6_out, or_7_out,
       or_8_out, or_9_out, or_10_out, or_11_out, or_12_out, or_14_out, or_16_out, or_17_out;
  wire [2:0] multiplexer_1_out;

  or or_1 (or_1_out, beq, bne, blez, bgtz, bltz, bgez);
  or or_2 (or_2_out, j, jal);
  or or_3 (or_3_out, jr, jalr);
  or or_4 (or_4_out, slt, slti);
  or or_5 (or_5_out, sltu, sltiu);
  and and_1 (and_1_out, R, not_1_out);
  not not_1 (not_1_out, jr);
  or or_6 (or_6_out, addiu, andi, ori, xori);
  or or_7 (or_7_out, lui, slti, sltiu);
  or or_8 (or_8_out, lb, lh, lw, lbu, lhu);
  or or_9 (or_9_out, \and , \or , \xor , \nor , andi, ori, xori);
  Priority_Encoder #(.select(2)) priority_encoder_1 (
    .in0(1'b1), .in1(or_9_out), .in2(or_10_out), .in3(or_11_out), .out(OPSel), .en_in(1'b1));  // open: gs, en_out
  or or_10 (or_10_out, sll, srl, sra, sllv, srlv, srav);
  or or_11 (or_11_out, slt, sltu, slti, sltiu);
  Priority_Encoder #(.select(2)) priority_encoder_2 (
    .in0(1'b1), .in1(or_12_out), .in2(lui), .in3(1'b0), .out(EXTSel), .en_in(1'b1));  // open: gs, en_out
  or or_12 (or_12_out, andi, ori, xori);
  Priority_Encoder #(.select(2)) priority_encoder_3 (
    .in0(1'b1), .in1(or_1_out), .in2(or_2_out), .in3(or_3_out), .out(NPCSel), .en_in(1'b1));  // open: gs, en_out
  Multiplexer #(.width(3), .enable("false")) multiplexer_1 (
    .in0(funct[2:0]), .in1(opcode[2:0]), .out(multiplexer_1_out), .sel(IJ));
  Multiplexer #(.select(2), .width(3), .enable("false")) multiplexer_2 (
    .in0({2'b00, subu}), .in1(multiplexer_1_out), .in2(funct[2:0]), .in3(3'b000), .out(FuncSel), .sel(OPSel));
  Priority_Encoder priority_encoder_4 (
    .in0(1'b1), .in1(bgez), .in2(or_4_out), .in3(or_5_out), .in4(beq), .in5(bne), .in6(blez), .in7(bgtz),
    .out(CompSel), .en_in(1'b1));  // open: gs, en_out
  or or_13 (GRFWE, and_1_out, or_6_out, or_7_out, or_8_out, or_14_out);
  or or_14 (or_14_out, jal, jalr);
  or or_15 (DMWE, sb, sh, sw);
  or or_16 (or_16_out, lb, lh, lw, lbu, lhu);
  or or_17 (or_17_out, jalr, jal);
  Priority_Encoder #(.select(2)) priority_encoder_5 (
    .in0(1'b1), .in1(R), .in2(IJ), .in3(jal), .out(GRFA3MUX), .en_in(1'b1));  // open: gs, en_out
  Priority_Encoder #(.select(2)) priority_encoder_6 (
    .in0(1'b1), .in1(lui), .in2(or_16_out), .in3(or_17_out), .out(GRFWDMUX), .en_in(1'b1));  // open: gs, en_out
  and and_2 (ALUrtMUX, IJ, nor_1_out);
  nor nor_1 (nor_1_out, beq, bne, blez, bgtz, bltz, bgez, jr, jalr, j, jal);

  assign DMSel = opcode[2:0];

  // Notes on the sheet:
  //   Inputs
  //   Outputs
endmodule
