// Logisim project question_1109_12_2.circ as structural Verilog: 1 circuit, main circuit swap
module swap (
  input  I1,
  input  I2,
  input  S,
  output _01,
  output _02
);

  wire and_1_out, and_2_out, and_3_out, and_4_out, not_1_out, not_2_out;

  not not_1 (not_1_out, S);
  not not_2 (not_2_out, S);
  and and_1 (and_1_out, I1, not_1_out);
  and and_2 (and_2_out, I2, S);
  and and_3 (and_3_out, I1, S);
  and and_4 (and_4_out, I2, not_2_out);
  or or_1 (_01, and_1_out, and_2_out);
  or or_2 (_02, and_3_out, and_4_out);

  // Other names for the same wires on the sheet: T1 = I1; T2 = I2; TS = S
endmodule
