// Logisim project question_1109_15_1.circ as structural Verilog: 1 circuit, main circuit main
module main (
  input  [2:0] N,
  output [3:0] Nth
);

  wire clock_1_out, clock_2_out, comparator_1_eq, comparator_2_eq, not_1_out, not_2_out;
  wire [2:0] counter_1_q;
  wire [3:0] adder_1_out, and_1_out, bit_extender_1_out, bit_extender_2_out, or_1_out, register_1_q,
       register_2_q;

  not not_1 (not_1_out, comparator_1_eq);
  Counter #(.width(3), .max('h7)) counter_1 (
    .count(not_1_out), .Q(counter_1_q), .clk(clock_1_out));  // open: load, D, carry, clr
  Clock clock_1 (.out(clock_1_out));
  Comparator #(.width(3), .mode("unsigned")) comparator_1 (
    .a(N), .b(counter_1_q), .eq(comparator_1_eq));  // open: gt, lt
  assign bit_extender_1_out = {{3{comparator_2_eq}}, comparator_2_eq};  // Bit_Extender bit_extender_1
  not not_2 (not_2_out, comparator_1_eq);
  assign or_1_out = adder_1_out | and_1_out;  // OR_Gate or_1, 4 bits wide
  assign and_1_out = 4'b0001 & bit_extender_1_out;  // AND_Gate and_1, 4 bits wide
  Register #(.width(4)) register_1 (
    .D(register_2_q), .en(not_2_out), .Q(register_1_q), .clk(clock_2_out));  // open: clr
  Clock clock_2 (.out(clock_2_out));
  Register #(.width(4)) register_2 (.D(or_1_out), .en(not_2_out), .Q(register_2_q), .clk(clock_2_out));  // open: clr
  assign bit_extender_2_out = {{3{comparator_1_eq}}, comparator_1_eq};  // Bit_Extender bit_extender_2
  Adder #(.width(4)) adder_1 (.a(register_1_q), .b(register_2_q), .out(adder_1_out));  // open: cin, cout
  Comparator #(.width(4), .mode("unsigned")) comparator_2 (
    .a(register_2_q), .b(4'b0000), .eq(comparator_2_eq));  // open: gt, lt
  assign Nth = bit_extender_2_out & register_2_q;  // AND_Gate and_2, 4 bits wide
endmodule
