// Logisim project question_1109_16.circ as structural Verilog: 4 circuits, main circuit 4bit_sort
module _4bit_sort (
  input  [3:0] I1,
  input  [3:0] I2,
  input  [3:0] I3,
  input  [3:0] I4,
  output [3:0] O1,
  output [3:0] O2,
  output [3:0] O3,
  output [3:0] O4
);

  wire [3:0] get_min_1_out_3, get_min_1_out_4, get_min_2_out_3, get_min_2_out_4, get_min_3_out_3,
       get_min_4_out_3, get_min_4_out_4, get_min_5_out_3;

  get_min get_min_1 (.n1(I1), .n2(I2), .out_3(get_min_1_out_3), .out_4(get_min_1_out_4));
  get_min get_min_2 (.n1(get_min_1_out_4), .n2(I3), .out_3(get_min_2_out_3), .out_4(get_min_2_out_4));
  get_min get_min_3 (.n1(get_min_2_out_4), .n2(I4), .out_3(get_min_3_out_3), .out_4(O4));
  get_min get_min_4 (.n1(get_min_1_out_3), .n2(get_min_2_out_3), .out_3(get_min_4_out_3), .out_4(get_min_4_out_4));
  get_min get_min_5 (.n1(get_min_4_out_4), .n2(get_min_3_out_3), .out_3(get_min_5_out_3), .out_4(O3));
  get_min get_min_6 (.n1(get_min_4_out_3), .n2(get_min_5_out_3), .out_3(O1), .out_4(O2));

  // Notes on the sheet:
  //   bubble_sort
endmodule

module _1bit_swap (
  input  I1,
  input  I2,
  input  S,
  output _01,
  output _02
);

  wire and_1_out, and_2_out, and_3_out, and_4_out, not_1_out, not_2_out;

  not not_1 (not_1_out, S);
  not not_2 (not_2_out, S);
  and and_1 (and_1_out, I1, not_1_out);
  and and_2 (and_2_out, I2, S);
  and and_3 (and_3_out, I1, S);
  and and_4 (and_4_out, I2, not_2_out);
  or or_1 (_01, and_1_out, and_2_out);
  or or_2 (_02, and_3_out, and_4_out);
endmodule

module _4bit_swap (
  input  [3:0] I1,
  input  S,
  input  [3:0] I2,
  output [3:0] out_4,
  output [3:0] out_5
);

  _1bit_swap b0 (.I1(I1[0]), .I2(I2[0]), .S(S), ._01(out_4[0]), ._02(out_5[0]));
  _1bit_swap b1 (.I1(I1[1]), .I2(I2[1]), .S(S), ._01(out_4[1]), ._02(out_5[1]));
  _1bit_swap b2 (.I1(I1[2]), .I2(I2[2]), .S(S), ._01(out_4[2]), ._02(out_5[2]));
  _1bit_swap b3 (.I1(I1[3]), .I2(I2[3]), .S(S), ._01(out_4[3]), ._02(out_5[3]));
endmodule

module get_min (
  input  [3:0] n1,
  input  [3:0] n2,
  output [3:0] out_3,
  output [3:0] out_4
);

  wire comparator_1_gt;

  Comparator #(.width(4), .mode("unsigned")) comparator_1 (.a(n1), .b(n2), .gt(comparator_1_gt));  // open: eq, lt
  _4bit_swap _4bit_swap (.I1(n1), .S(comparator_1_gt), .out_4(out_3), .I2(n2), .out_5(out_4));
endmodule
