// Logisim project question_1109_22.circ as structural Verilog: 2 circuits, main circuit mod5
module mod5 (
  input  In,
  output S0,
  output S1,
  output S2,
  output S3,
  output S4
);

  wire and_1_out, and_2_out, and_3_out, and_4_out, and_5_out, and_6_out, clock_1_out, not_1_out, not_2_out,
       not_3_out, not_4_out, not_5_out, not_6_out, not_7_out, not_8_out;
  wire [1:0] or_2_out, register_1_q;

  not not_1 (not_1_out, register_1_q[1]);
  not not_2 (not_2_out, register_1_q[0]);
  not not_3 (not_3_out, register_1_q[1]);
  not not_4 (not_4_out, register_1_q[0]);
  not not_5 (not_5_out, register_1_q[1]);
  not not_6 (not_6_out, In);
  not not_7 (not_7_out, register_1_q[0]);
  not not_8 (not_8_out, In);
  and and_1 (and_1_out, not_1_out, register_1_q[0]);
  and and_2 (and_2_out, register_1_q[1], not_2_out);
  and and_3 (and_3_out, not_3_out, not_4_out, In);
  and and_4 (and_4_out, not_5_out, register_1_q[0], not_6_out);
  and and_5 (and_5_out, register_1_q[1], not_7_out, not_8_out);
  and and_6 (and_6_out, register_1_q[1], register_1_q[0], In);
  or or_1 (or_2_out[1], and_1_out, and_2_out);
  or or_2 (or_2_out[0], and_3_out, and_4_out, and_5_out, and_6_out);
  Register #(.width(2)) register_1 (.D(or_2_out), .Q(register_1_q), .clk(clock_1_out));  // open: en, clr
  Clock clock_1 (.out(clock_1_out));
  Decoder #(.select(2), .enable("false")) decoder_1 (.out0(S1), .out1(S2), .out2(S3), .out3(S4), .sel(or_2_out));

  assign S0 = 1'b0;
endmodule

module test (
  output In,
  output S0,
  output S1,
  output S2,
  output S3,
  output S4,
  output out_7
);

  wire clock_1_out;
  wire [3:0] counter_1_q;

  Counter #(.width(4), .max('hf)) counter_1 (
    .Q(counter_1_q), .carry(out_7), .clk(clock_1_out));  // open: load, D, count, clr
  Clock clock_1 (.out(clock_1_out));
  ROM #(.addrWidth(4), .dataWidth(1)) rom_1 (.addr(counter_1_q), .data(In));  // open: sel
  mod5 mod5_1 (.In(In), .S0(S0), .S1(S1), .S2(S2), .S3(S3), .S4(S4));

  // Notes on the sheet:
  //   contents of rom_1 (hex, n*v repeats v):
  //   0 1 0 0 1 0 0 1 0 0 1 0 0 1
endmodule
