// Logisim project question_1109_22_wrong.circ as structural Verilog: 2 circuits, main circuit mod5
module mod5 (
  input  In,
  output S0,
  output S1,
  output S2,
  output S3,
  output S4
);

  wire and_1_out, and_2_out, and_3_out, and_4_out, and_5_out, and_6_out, and_7_out, and_8_out, and_9_out,
       clock_1_out, not_1_out, not_2_out, not_3_out, not_4_out, not_5_out, not_6_out, not_7_out, not_8_out;
  wire [2:0] or_3_out, register_1_q;

  not not_1 (not_1_out, register_1_q[0]);
  not not_2 (not_2_out, In);
  not not_3 (not_3_out, register_1_q[1]);
  not not_4 (not_4_out, In);
  not not_5 (not_5_out, register_1_q[2]);
  not not_6 (not_6_out, register_1_q[1]);
  not not_7 (not_7_out, In);
  not not_8 (not_8_out, In);
  and and_1 (and_1_out, register_1_q[1], not_1_out, not_2_out);
  and and_2 (and_2_out, register_1_q[2], In);
  and and_3 (and_3_out, not_3_out, register_1_q[0]);
  and and_4 (and_4_out, register_1_q[0], In);
  and and_5 (and_5_out, register_1_q[2], not_4_out);
  and and_6 (and_6_out, not_5_out, not_6_out, In);
  and and_7 (and_7_out, register_1_q[1], register_1_q[0], not_7_out);
  and and_8 (and_8_out, register_1_q[2], not_8_out);
  and and_9 (and_9_out, register_1_q[2], register_1_q[0]);
  or or_1 (or_3_out[2], and_1_out, and_2_out);
  or or_2 (or_3_out[1], and_3_out, and_4_out, and_5_out);
  or or_3 (or_3_out[0], and_6_out, and_7_out, and_8_out, and_9_out);
  Register #(.width(3)) register_1 (.D(or_3_out), .Q(register_1_q), .clk(clock_1_out));  // open: en, clr
  Clock clock_1 (.out(clock_1_out));
  Decoder #(.select(3), .enable("false")) decoder_1 (
    .out0(S0), .out1(S1), .out2(S2), .out3(S3), .out4(S4), .sel(or_3_out));  // open: out5, out6, out7
endmodule

module test (
  output out_1,
  output out_2,
  output out_3,
  output out_4,
  output out_5,
  output out_6,
  output out_7
);

  wire clock_1_out;
  wire [3:0] counter_1_q;

  Clock clock_1 (.out(clock_1_out));
  Counter #(.width(4), .max('hf)) counter_1 (
    .Q(counter_1_q), .carry(out_7), .clk(clock_1_out));  // open: load, D, count, clr
  ROM #(.addrWidth(4), .dataWidth(1)) rom_1 (.addr(counter_1_q), .data(out_1));  // open: sel
  mod5 mod5_1 (.In(out_1), .S0(out_2), .S1(out_3), .S2(out_4), .S3(out_5), .S4(out_6));

  // Notes on the sheet:
  //   contents of rom_1 (hex, n*v repeats v):
  //   0 1 0 0 1 0 0 1 0 0 1 0 0 1
endmodule
