// Logisim project question_1109_23.circ as structural Verilog: 5 circuits, main circuit 幂次矩阵生成
module main (
  input  [31:0] in_1,
  output [31:0] out_2
);

  wire Clock, comparator_1_eq, Continue, InitFinish, nowbit;
  wire [31:0] multiplexer_1_out, n11, n12, n21, n22, p11, p12, p21, p22, register_1_q, shifter_1_out,
       \矩阵乘法_1_out_9 , \矩阵乘法_1_out_10 , \矩阵乘法_1_out_11 , \矩阵乘法_1_out_12 , \矩阵寄存_1_a11out , \矩阵寄存_1_a12out ,
       \矩阵寄存_1_a21out , \矩阵寄存_1_a22out , \矩阵选择_1_out_10 , \矩阵选择_1_out_11 , \矩阵选择_1_out_12 , \矩阵选择_1_out_13 ;

  Clock clock_1 (.out(Clock));
  Multiplexer #(.width(32), .enable("false")) multiplexer_1 (
    .in0(in_1), .in1(shifter_1_out), .out(multiplexer_1_out), .sel(InitFinish));
  \矩阵选择  \u_矩阵选择_1  (
    .select(InitFinish), .in_2(32'h1), .in_3({32{1'b0}}), .in_4({32{1'b0}}), .in_5(32'h1), .in_6(p11),
    .in_7(p12), .in_8(p21), .in_9(p22), .out_10(\矩阵选择_1_out_10 ), .out_11(\矩阵选择_1_out_11 ),
    .out_12(\矩阵选择_1_out_12 ), .out_13(\矩阵选择_1_out_13 ));
  D_Flip_Flop d_ff_1 (.clk(Clock), .D(1'b1), .Q(InitFinish));  // open: Qn, preset, en, reset
  Register #(.width(32)) register_1 (.D(multiplexer_1_out), .Q(register_1_q), .clk(Clock));  // open: en, clr
  \矩阵寄存  \u_矩阵寄存_1  (
    .clock(Clock), .a11out(\矩阵寄存_1_a11out ), .a12out(\矩阵寄存_1_a12out ), .a21out(\矩阵寄存_1_a21out ),
    .a22out(\矩阵寄存_1_a22out ), .a11next(\矩阵选择_1_out_10 ), .a21next(\矩阵选择_1_out_12 ),
    .a12next(\矩阵选择_1_out_11 ), .a22next(\矩阵选择_1_out_13 ));
  Shifter #(.width(32), .shift("lr")) shifter_1 (.in(register_1_q), .\dist (5'b00001), .out(shifter_1_out));
  BitSelector #(.width(32)) bitselector_1 (.in(register_1_q), .out(nowbit), .sel({5{1'b0}}));
  Comparator #(.width(32), .mode("unsigned")) comparator_1 (
    .a(register_1_q), .b({32{1'b0}}), .eq(comparator_1_eq));  // open: gt, lt
  not not_1 (Continue, comparator_1_eq);
  Multiplexer #(.width(32), .enable("false")) multiplexer_2 (
    .in0(\矩阵寄存_1_a12out ), .in1({32{1'b0}}), .out(out_2), .sel(Continue));
  \矩阵乘法  \u_矩阵乘法_1  (
    .in_1(\矩阵寄存_1_a11out ), .in_2(\矩阵寄存_1_a12out ), .in_3(\矩阵寄存_1_a21out ), .in_4(\矩阵寄存_1_a22out ),
    .out_9(\矩阵乘法_1_out_9 ), .out_10(\矩阵乘法_1_out_10 ), .out_11(\矩阵乘法_1_out_11 ), .out_12(\矩阵乘法_1_out_12 ),
    .in_5(n11), .in_6(n12), .in_7(n21), .in_8(n22));
  \矩阵选择  \u_矩阵选择_2  (
    .select(nowbit), .in_2(\矩阵寄存_1_a11out ), .in_3(\矩阵寄存_1_a12out ), .in_4(\矩阵寄存_1_a21out ),
    .in_5(\矩阵寄存_1_a22out ), .in_6(\矩阵乘法_1_out_9 ), .in_7(\矩阵乘法_1_out_10 ), .in_8(\矩阵乘法_1_out_11 ),
    .in_9(\矩阵乘法_1_out_12 ), .out_10(p11), .out_11(p12), .out_12(p21), .out_13(p22));
  \幂次矩阵生成  \u_幂次矩阵生成_1  (.a11out(n11), .a12out(n12), .a21out(n21), .a22out(n22), .in_1(Clock), .in_2(InitFinish));
endmodule

module \幂次矩阵生成  (
  input  in_1,
  input  in_2,
  output [31:0] a11out,
  output [31:0] a12out,
  output [31:0] a21out,
  output [31:0] a22out
);

  wire [31:0] a11next, a11result, a12next, a12result, a21next, a21result, a22next, a22result;

  \矩阵寄存  \u_矩阵寄存_1  (
    .clock(in_1), .a11out(a11out), .a12out(a12out), .a21out(a21out), .a22out(a22out), .a11next(a11next),
    .a21next(a21next), .a12next(a12next), .a22next(a22next));
  \矩阵选择  \u_矩阵选择_1  (
    .select(in_2), .in_2(32'h1), .in_3(32'h1), .in_4(32'h1), .in_5({32{1'b0}}), .in_6(a11result),
    .in_7(a12result), .in_8(a21result), .in_9(a22result), .out_10(a11next), .out_11(a12next),
    .out_12(a21next), .out_13(a22next));
  \矩阵乘法  \u_矩阵乘法_1  (
    .in_1(a11out), .in_2(a12out), .in_3(a21out), .in_4(a22out), .out_9(a11result), .out_10(a12result),
    .out_11(a21result), .out_12(a22result), .in_5(a11out), .in_6(a12out), .in_7(a21out), .in_8(a22out));

  // Other names for the same wires on the sheet: a11[31:0] = a11out; a12[31:0] = a12out; a21[31:0] = a21out;
  //   a22[31:0] = a22out; clock = in_1; InitFinish = in_2
endmodule

module \矩阵乘法  (
  input  [31:0] in_1,
  input  [31:0] in_2,
  input  [31:0] in_3,
  input  [31:0] in_4,
  input  [31:0] in_5,
  input  [31:0] in_6,
  input  [31:0] in_7,
  input  [31:0] in_8,
  output [31:0] out_9,
  output [31:0] out_10,
  output [31:0] out_11,
  output [31:0] out_12
);

  wire [31:0] multiplier_1_out, multiplier_2_out, multiplier_3_out, multiplier_4_out, multiplier_5_out,
       multiplier_6_out, multiplier_7_out, multiplier_8_out;

  Multiplier #(.width(32)) multiplier_1 (.a(in_1), .b(in_5), .out(multiplier_1_out));  // open: cin, cout
  Multiplier #(.width(32)) multiplier_2 (.a(in_2), .b(in_7), .out(multiplier_2_out));  // open: cin, cout
  Multiplier #(.width(32)) multiplier_3 (.a(in_3), .b(in_5), .out(multiplier_3_out));  // open: cin, cout
  Multiplier #(.width(32)) multiplier_4 (.a(in_4), .b(in_7), .out(multiplier_4_out));  // open: cin, cout
  Adder #(.width(32)) adder_1 (.a(multiplier_1_out), .b(multiplier_2_out), .out(out_9));  // open: cin, cout
  Adder #(.width(32)) adder_2 (.a(multiplier_3_out), .b(multiplier_4_out), .out(out_11));  // open: cin, cout
  Multiplier #(.width(32)) multiplier_5 (.a(in_1), .b(in_6), .out(multiplier_5_out));  // open: cin, cout
  Multiplier #(.width(32)) multiplier_6 (.a(in_2), .b(in_8), .out(multiplier_6_out));  // open: cin, cout
  Multiplier #(.width(32)) multiplier_7 (.a(in_3), .b(in_6), .out(multiplier_7_out));  // open: cin, cout
  Multiplier #(.width(32)) multiplier_8 (.a(in_4), .b(in_8), .out(multiplier_8_out));  // open: cin, cout
  Adder #(.width(32)) adder_3 (.a(multiplier_5_out), .b(multiplier_6_out), .out(out_10));  // open: cin, cout
  Adder #(.width(32)) adder_4 (.a(multiplier_7_out), .b(multiplier_8_out), .out(out_12));  // open: cin, cout

  // Other names for the same wires on the sheet: a11[31:0] = in_1; a12[31:0] = in_2; a21[31:0] = in_3;
  //   a22[31:0] = in_4; b11[31:0] = in_5; b12[31:0] = in_6; b21[31:0] = in_7; b22[31:0] = in_8; c11[31:0] = out_9;
  //   c12[31:0] = out_10; c21[31:0] = out_11; c22[31:0] = out_12
endmodule

module \矩阵寄存  (
  input  clock,
  input  [31:0] a11next,
  input  [31:0] a12next,
  input  [31:0] a21next,
  input  [31:0] a22next,
  output [31:0] a11out,
  output [31:0] a12out,
  output [31:0] a21out,
  output [31:0] a22out
);

  Register #(.width(32)) Fn_1 (.D(a11next), .en(1'b1), .Q(a11out), .clk(clock));  // open: clr
  Register #(.width(32)) Fn (.D(a21next), .en(1'b1), .Q(a21out), .clk(clock));  // open: clr
  Register #(.width(32)) Fn_2 (.D(a12next), .en(1'b1), .Q(a12out), .clk(clock));  // open: clr
  Register #(.width(32)) Fn_1_2 (.D(a22next), .en(1'b1), .Q(a22out), .clk(clock));  // open: clr
endmodule

module \矩阵选择  (
  input  select,
  input  [31:0] in_2,
  input  [31:0] in_3,
  input  [31:0] in_4,
  input  [31:0] in_5,
  input  [31:0] in_6,
  input  [31:0] in_7,
  input  [31:0] in_8,
  input  [31:0] in_9,
  output [31:0] out_10,
  output [31:0] out_11,
  output [31:0] out_12,
  output [31:0] out_13
);

  Multiplexer #(.width(32), .enable("false")) multiplexer_1 (.in0(in_2), .in1(in_6), .out(out_10), .sel(select));
  Multiplexer #(.width(32), .enable("false")) multiplexer_2 (.in0(in_4), .in1(in_8), .out(out_12), .sel(select));
  Multiplexer #(.width(32), .enable("false")) multiplexer_3 (.in0(in_3), .in1(in_7), .out(out_11), .sel(select));
  Multiplexer #(.width(32), .enable("false")) multiplexer_4 (.in0(in_5), .in1(in_9), .out(out_13), .sel(select));

  // Other names for the same wires on the sheet: a11[31:0] = in_2; a12[31:0] = in_3; a21[31:0] = in_4;
  //   a22[31:0] = in_5; b11[31:0] = in_6; b12[31:0] = in_7; b21[31:0] = in_8; b22[31:0] = in_9; c11[31:0] = out_10;
  //   c12[31:0] = out_11; c21[31:0] = out_12; c22[31:0] = out_13
endmodule
